// Logisim project exo2-5.circ as structural Verilog: 1 circuit, main circuit main
module main (
  input  [3:0] t3t2t1t0,
  output r1,
  output o1,
  output v1,
  output r2,
  output o2,
  output v2
);

  wire and_2_out, and_3_out, and_5_out, and_6_out;

  not not_1 (r1, t3t2t1t0[3]);
  and and_1 (o1, t3t2t1t0[3], t3t2t1t0[2], t3t2t1t0[1]);
  or or_1 (v1, and_2_out, and_3_out);
  and and_2 (and_2_out, t3t2t1t0[3], ~t3t2t1t0[1]);  // AND_Gate
  and and_3 (and_3_out, t3t2t1t0[3], ~t3t2t1t0[0]);  // AND_Gate
  and and_4 (o2, ~t3t2t1t0[3], t3t2t1t0[2], t3t2t1t0[1]);  // AND_Gate
  and and_5 (and_5_out, ~t3t2t1t0[3], ~t3t2t1t0[1]);  // AND_Gate
  or or_2 (v2, and_5_out, and_6_out);
  and and_6 (and_6_out, ~t3t2t1t0[3], ~t3t2t1t0[2]);  // AND_Gate

  assign r2 = t3t2t1t0[3];
endmodule
