// Logisim project exo4.circ as structural Verilog: 2 circuits, main circuit q3
module q3 (
  input  [2:0] d1d2d3,
  output A,
  output P1,
  output P2,
  output P3
);

  wire and_1_out, and_2_out, and_3_out, and_6_out, and_7_out;

  and and_1 (and_1_out, ~d1d2d3[2], d1d2d3[0]);  // AND_Gate
  or or_1 (A, and_1_out, and_3_out, and_2_out);
  and and_2 (and_2_out, ~d1d2d3[1], d1d2d3[0]);  // AND_Gate
  and and_3 (and_3_out, ~d1d2d3[2], d1d2d3[1]);  // AND_Gate
  and and_4 (P1, ~d1d2d3[2], ~d1d2d3[2], ~d1d2d3[2]);  // AND_Gate
  and and_5 (P2, ~d1d2d3[1], ~d1d2d3[0]);  // AND_Gate
  and and_6 (and_6_out, d1d2d3[2], ~d1d2d3[0]);  // AND_Gate
  or or_2 (P3, and_6_out, and_7_out);
  and and_7 (and_7_out, ~d1d2d3[1], ~d1d2d3[0]);  // AND_Gate
endmodule

module q6 (
  input  [3:0] d1d2d3A,
  output P_prime_1,
  output P_prime_2,
  output P_prime_3,
  output ALERTE
);

  wire and_2_out, and_3_out, and_5_out, and_6_out, and_7_out, and_8_out, and_9_out, and_10_out, and_11_out,
       and_12_out, or_3_out;

  and and_1 (P_prime_1, and_2_out, and_3_out);
  and and_2 (and_2_out, ~d1d2d3A[3], ~d1d2d3A[2]);  // AND_Gate
  and and_3 (and_3_out, ~d1d2d3A[1], ~d1d2d3A[0]);  // AND_Gate
  and and_4 (P_prime_2, and_5_out, ~d1d2d3A[0]);  // AND_Gate
  and and_5 (and_5_out, ~d1d2d3A[1], ~d1d2d3A[2]);  // AND_Gate
  or or_1 (P_prime_3, and_6_out, and_7_out);
  and and_6 (and_6_out, and_8_out, ~d1d2d3A[0]);  // AND_Gate
  and and_7 (and_7_out, ~d1d2d3A[2], and_9_out);  // AND_Gate
  and and_8 (and_8_out, d1d2d3A[3], ~d1d2d3A[1]);  // AND_Gate
  and and_9 (and_9_out, ~d1d2d3A[1], ~d1d2d3A[0]);  // AND_Gate
  or or_2 (ALERTE, or_3_out, and_10_out);
  and and_10 (and_10_out, ~d1d2d3A[2], d1d2d3A[1]);  // AND_Gate
  or or_3 (or_3_out, and_11_out, and_12_out);
  and and_11 (and_11_out, ~d1d2d3A[3], d1d2d3A[1]);  // AND_Gate
  and and_12 (and_12_out, ~d1d2d3A[3], d1d2d3A[2]);  // AND_Gate

  // Notes on the sheet:
  //   d1
  //   A
  //   d3
  //   d2
endmodule
