// Logisim project exo1-2.circ as structural Verilog: 1 circuit, main circuit main
module main (
  input  a,
  input  b,
  input  c,
  input  d,
  output out_5
);

  wire a_et_c_out, b_et_c_out, c_et_non_d_out, non_b_et_non_d_out;

  and non_b_et_non_d (non_b_et_non_d_out, ~b, ~d);  // AND_Gate
  or la_disjonction_de_tout_les__et (out_5, non_b_et_non_d_out, b_et_c_out, a_et_c_out, c_et_non_d_out);
  and b_et_c (b_et_c_out, b, c);
  and a_et_c (a_et_c_out, a, c);
  and c_et_non_d (c_et_non_d_out, b, ~d);  // AND_Gate
endmodule
