// Logisim project exo 2 tp7.circ as structural Verilog
module N2G4 (
  input  [3:0] n3n2n1n0,
  output [3:0] g3g2g1g0
);

  xor xor_1 (g3g2g1g0[0], n3n2n1n0[0], n3n2n1n0[1]);
  xor xor_2 (g3g2g1g0[1], n3n2n1n0[1], n3n2n1n0[2]);
  xor xor_3 (g3g2g1g0[2], n3n2n1n0[2], n3n2n1n0[3]);

  assign g3g2g1g0[3] = n3n2n1n0[3];
endmodule
