// Logisim project ksi td1exo5 forme normal.circ as structural Verilog: 1 circuit, main circuit main
module main (
  input  a,
  input  b,
  input  c,
  output out_4
);

  wire nand_1_out, nand_2_out, nand_3_out;

  nand nand_1 (nand_1_out, ~a, ~b, c);  // NAND_Gate
  nand nand_2 (nand_2_out, ~a, b, ~c);  // NAND_Gate
  nand nand_3 (nand_3_out, a, b, ~c);  // NAND_Gate
  nand nand_4 (out_4, nand_1_out, nand_2_out, nand_3_out);

  // Notes on the sheet:
  //   a
  //   b
  //   c
  //   a
  //   b
  //   c
endmodule
