// Logisim project shadok.circ as structural Verilog
module shad1 (
  input  [1:0] a1a0
);

  wire and_4_out, or_4_out, or_5_out, or_6_out;
  wire [1:0] or_3_out;
  wire [2:0] or_2_out;
  wire [3:0] or_1_out, or_8_out;

  and and_1 (or_2_out[1], a1a0[0], a1a0[0]);
  and and_2 (or_8_out[3], ~a1a0[0], a1a0[1]);  // AND_Gate
  and and_3 (or_1_out[2], ~a1a0[0], ~a1a0[1]);  // AND_Gate
  and and_4 (and_4_out, a1a0[0], ~a1a0[1]);  // AND_Gate
  or or_1 (or_1_out[0], and_4_out, or_8_out[3]);
  or or_2 (or_2_out[0], or_8_out[3], or_4_out);
  buf or_3 (or_3_out[0], or_5_out);  // OR_Gate
  or or_4 (or_4_out, or_1_out[2], and_4_out);
  or or_5 (or_5_out, or_8_out[3], or_6_out);
  DotMatrix #(.matrixcols(4), .matrixrows(4)) dotmatrix_1 (
    .col0({or_1_out[3:2], or_1_out[2], or_1_out[0]}), .col1({or_1_out[2], or_2_out}),
    .col2({or_1_out[2], or_2_out[1], or_3_out}), .col3(or_8_out));
  or or_6 (or_6_out, or_1_out[2], and_4_out);
  or or_7 (or_8_out[2], or_8_out[3], or_1_out[2]);
  or or_8 (or_8_out[0], or_8_out[3], and_4_out);
  or or_9 (or_8_out[1], or_8_out[3], or_1_out[2]);
endmodule
